// Logisim project CPU_v24 bits.circ as structural Verilog: 1 circuit, main circuit main
module main (
);

  wire adder_1_cout, adder_5_cout, adder_6_cout, and_1_out, and_2_out, and_3_out, and_5_out, clock_1_out,
       demultiplexer_1_out0, demultiplexer_1_out1, demultiplexer_1_out2, demultiplexer_1_out3,
       demultiplexer_1_out4, demultiplexer_1_out5, demultiplexer_1_out6, demultiplexer_1_out7,
       demultiplexer_1_out8, demultiplexer_1_out9, demultiplexer_1_out10, demultiplexer_1_out11,
       demultiplexer_1_out12, demultiplexer_1_out13, demultiplexer_1_out14, demultiplexer_1_out15,
       demultiplexer_5_out0, demultiplexer_5_out1, GLOBAL_RESET_out, multiplexer_4_out, multiplexer_5_out,
       multiplexer_6_out, multiplexer_8_out, multiplexer_9_out, not_2_out, OFFSET_X_carry, OFFSET_Y_carry,
       or_1_out, or_5_out, or_6_out, or_7_out, subtractor_1_bout, xnor_1_out, xor_1_out, xor_2_out, xor_3_out;
  wire [1:0] demultiplexer_4_out2_2, demultiplexer_4_out3_2;
  wire [2:0] adder_5_out, adder_6_out, CODE_ROM_data_4, CODE_ROM_data_7, OFFSET_X_q, OFFSET_X_q_2,
       OFFSET_Y_q, OFFSET_Y_q_2;
  wire [3:0] adder_3_out, adder_4_out, bit_extender_1_out, bit_extender_2_out, FLAGS_q, RESOURCES_data;
  wire [3:1] comparator_1_eq;
  wire [4:0] demultiplexer_3_out6, demultiplexer_3_out7;
  wire [4:3] CODE_ROM_data_5;
  wire [5:0] PIXEL_OFFSET_q;
  wire [5:3] CODE_ROM_data_8;
  wire [6:0] demultiplexer_4_out3;
  wire [7:0] A_out, multiplexer_10_out_2, multiplexer_11_out, RINPT_q, STACK_POINTER_q, TILE_OFFSET_q;
  wire [8:0] CODE_ROM_data_3, demultiplexer_4_out1, demultiplexer_4_out2, demultiplexer_4_out4;
  wire [9:0] multiplexer_10_out;
  wire [15:0] adder_7_out, bit_extender_4_out, LUT_data, shifter_3_out, TILE_BUFFER_dout;
  wire [15:6] multiplexer_10_out_3;
  wire [23:0] adder_1_out, adder_2_out, and_4_out, bit_extender_3_out, CODE_ROM_data,
       controlled_buffer_1_out, controlled_buffer_2_out, controlled_buffer_3_out, controlled_buffer_4_out,
       counter_1_q, demultiplexer_2_out0, demultiplexer_2_out1, demultiplexer_2_out2, demultiplexer_2_out3,
       demultiplexer_2_out4, demultiplexer_2_out5, demultiplexer_2_out6, demultiplexer_2_out7,
       demultiplexer_3_out0, demultiplexer_3_out1, demultiplexer_3_out2, demultiplexer_3_out3,
       demultiplexer_3_out4, GEN_RAM_dout, multiplexer_1_out, multiplexer_2_out, multiplexer_3_out,
       multiplexer_7_out, not_1_out, or_4_out, R0_q, R1_q, R2_q, R3_q, R4_q, R5_q, R6_q, R7_q, R8_q, R9_q,
       R10_q, R11_q, R12_q, R13_q, R14_q, R15_q, shifter_1_out, shifter_2_out, STACK_dout, subtractor_1_out,
       xor_4_out;
  wire [23:5] demultiplexer_3_out6_2, demultiplexer_3_out7_2;
  wire [25:14] CODE_ROM_data_6;
  wire [31:24] CODE_ROM_data_2;

  or or_1 (or_1_out, demultiplexer_4_out1[0], demultiplexer_4_out2[0]);
  Demultiplexer #(.select(4)) demultiplexer_1 (
    .out0(demultiplexer_1_out0), .out1(demultiplexer_1_out1), .out2(demultiplexer_1_out2),
    .out3(demultiplexer_1_out3), .out4(demultiplexer_1_out4), .out5(demultiplexer_1_out5),
    .out6(demultiplexer_1_out6), .out7(demultiplexer_1_out7), .out8(demultiplexer_1_out8),
    .out9(demultiplexer_1_out9), .out10(demultiplexer_1_out10), .out11(demultiplexer_1_out11),
    .out12(demultiplexer_1_out12), .out13(demultiplexer_1_out13), .out14(demultiplexer_1_out14),
    .out15(demultiplexer_1_out15), .in(or_1_out), .sel(CODE_ROM_data_6[25:22]));
  Clock clock_1 (.out(clock_1_out));
  Button GLOBAL_RESET (.out(GLOBAL_RESET_out));
  Register #(.width(24)) R0 (
    .D({multiplexer_10_out_3, multiplexer_10_out_2[7:4], multiplexer_10_out[9:7], multiplexer_10_out_2[3:0], multiplexer_10_out[2:0]}),
    .en(demultiplexer_1_out0), .Q(R0_q), .clk(clock_1_out), .clr(GLOBAL_RESET_out));
  Register #(.width(24)) R4 (
    .D({multiplexer_10_out_3, multiplexer_10_out_2[7:4], multiplexer_10_out[9:7], multiplexer_10_out_2[3:0], multiplexer_10_out[2:0]}),
    .en(demultiplexer_1_out4), .Q(R4_q), .clk(clock_1_out), .clr(GLOBAL_RESET_out));
  Register #(.width(24)) R8 (
    .D({multiplexer_10_out_3, multiplexer_10_out_2[7:4], multiplexer_10_out[9:7], multiplexer_10_out_2[3:0], multiplexer_10_out[2:0]}),
    .en(demultiplexer_1_out8), .Q(R8_q), .clk(clock_1_out), .clr(GLOBAL_RESET_out));
  Register #(.width(24)) R12 (
    .D({multiplexer_10_out_3, multiplexer_10_out_2[7:4], multiplexer_10_out[9:7], multiplexer_10_out_2[3:0], multiplexer_10_out[2:0]}),
    .en(demultiplexer_1_out12), .Q(R12_q), .clk(clock_1_out), .clr(GLOBAL_RESET_out));
  assign controlled_buffer_1_out = demultiplexer_4_out1[1] ? multiplexer_2_out : 24'bz;  // Controlled_Buffer controlled_buffer_1
  assign controlled_buffer_2_out = demultiplexer_4_out1[1] ? multiplexer_3_out : 24'bz;  // Controlled_Buffer controlled_buffer_2
  and and_1 (and_1_out, xor_1_out, xnor_1_out);
  Demultiplexer #(.select(3), .width(24)) demultiplexer_2 (
    .out0(demultiplexer_2_out0), .out1(demultiplexer_2_out1), .out2(demultiplexer_2_out2),
    .out3(demultiplexer_2_out3), .out4(demultiplexer_2_out4), .out5(demultiplexer_2_out5),
    .out6(demultiplexer_2_out6), .out7(demultiplexer_2_out7), .in(controlled_buffer_1_out),
    .sel(demultiplexer_4_out1[6:4]));
  Demultiplexer #(.select(3), .width(24)) demultiplexer_3 (
    .out0(demultiplexer_3_out0), .out1(demultiplexer_3_out1), .out2(demultiplexer_3_out2),
    .out3(demultiplexer_3_out3), .out4(demultiplexer_3_out4),
    .out6({demultiplexer_3_out6_2, demultiplexer_3_out6}),
    .out7({demultiplexer_3_out7_2, demultiplexer_3_out7}), .in(controlled_buffer_2_out),
    .sel(demultiplexer_4_out1[6:4]));  // open: out5
  Register #(.width(24)) R1 (
    .D({multiplexer_10_out_3, multiplexer_10_out_2[7:4], multiplexer_10_out[9:7], multiplexer_10_out_2[3:0], multiplexer_10_out[2:0]}),
    .en(demultiplexer_1_out1), .Q(R1_q), .clk(clock_1_out), .clr(GLOBAL_RESET_out));
  Register #(.width(24)) R5 (
    .D({multiplexer_10_out_3, multiplexer_10_out_2[7:4], multiplexer_10_out[9:7], multiplexer_10_out_2[3:0], multiplexer_10_out[2:0]}),
    .en(demultiplexer_1_out5), .Q(R5_q), .clk(clock_1_out), .clr(GLOBAL_RESET_out));
  Register #(.width(24)) R9 (
    .D({multiplexer_10_out_3, multiplexer_10_out_2[7:4], multiplexer_10_out[9:7], multiplexer_10_out_2[3:0], multiplexer_10_out[2:0]}),
    .en(demultiplexer_1_out9), .Q(R9_q), .clk(clock_1_out), .clr(GLOBAL_RESET_out));
  Register #(.width(24)) R13 (
    .D({multiplexer_10_out_3, multiplexer_10_out_2[7:4], multiplexer_10_out[9:7], multiplexer_10_out_2[3:0], multiplexer_10_out[2:0]}),
    .en(demultiplexer_1_out13), .Q(R13_q), .clk(clock_1_out), .clr(GLOBAL_RESET_out));
  xor xor_1 (xor_1_out, multiplexer_1_out[23], demultiplexer_2_out0[23]);
  xnor xnor_1 (xnor_1_out, demultiplexer_3_out0[23], demultiplexer_2_out0[23]);
  and and_2 (and_2_out, FLAGS_q[2], demultiplexer_4_out1[3]);
  Register #(.width(24)) R2 (
    .D({multiplexer_10_out_3, multiplexer_10_out_2[7:4], multiplexer_10_out[9:7], multiplexer_10_out_2[3:0], multiplexer_10_out[2:0]}),
    .en(demultiplexer_1_out2), .Q(R2_q), .clk(clock_1_out), .clr(GLOBAL_RESET_out));
  Register #(.width(24)) R6 (
    .D({multiplexer_10_out_3, multiplexer_10_out_2[7:4], multiplexer_10_out[9:7], multiplexer_10_out_2[3:0], multiplexer_10_out[2:0]}),
    .en(demultiplexer_1_out6), .Q(R6_q), .clk(clock_1_out), .clr(GLOBAL_RESET_out));
  Register #(.width(24)) R10 (
    .D({multiplexer_10_out_3, multiplexer_10_out_2[7:4], multiplexer_10_out[9:7], multiplexer_10_out_2[3:0], multiplexer_10_out[2:0]}),
    .en(demultiplexer_1_out10), .Q(R10_q), .clk(clock_1_out), .clr(GLOBAL_RESET_out));
  Register #(.width(24)) R14 (
    .D({multiplexer_10_out_3, multiplexer_10_out_2[7:4], multiplexer_10_out[9:7], multiplexer_10_out_2[3:0], multiplexer_10_out[2:0]}),
    .en(demultiplexer_1_out14), .Q(R14_q), .clk(clock_1_out), .clr(GLOBAL_RESET_out));
  or or_2 (comparator_1_eq[3], and_1_out, and_3_out);
  Register #(.width(24)) R3 (
    .D({multiplexer_10_out_3, multiplexer_10_out_2[7:4], multiplexer_10_out[9:7], multiplexer_10_out_2[3:0], multiplexer_10_out[2:0]}),
    .en(demultiplexer_1_out3), .Q(R3_q), .clk(clock_1_out), .clr(GLOBAL_RESET_out));
  Register #(.width(24)) R7 (
    .D({multiplexer_10_out_3, multiplexer_10_out_2[7:4], multiplexer_10_out[9:7], multiplexer_10_out_2[3:0], multiplexer_10_out[2:0]}),
    .en(demultiplexer_1_out7), .Q(R7_q), .clk(clock_1_out), .clr(GLOBAL_RESET_out));
  Register #(.width(24)) R11 (
    .D({multiplexer_10_out_3, multiplexer_10_out_2[7:4], multiplexer_10_out[9:7], multiplexer_10_out_2[3:0], multiplexer_10_out[2:0]}),
    .en(demultiplexer_1_out11), .Q(R11_q), .clk(clock_1_out), .clr(GLOBAL_RESET_out));
  Register #(.width(24)) R15 (
    .D({multiplexer_10_out_3, multiplexer_10_out_2[7:4], multiplexer_10_out[9:7], multiplexer_10_out_2[3:0], multiplexer_10_out[2:0]}),
    .en(demultiplexer_1_out15), .Q(R15_q), .clk(clock_1_out), .clr(GLOBAL_RESET_out));
  xor xor_2 (xor_2_out, multiplexer_1_out[23], demultiplexer_2_out1[23]);
  and and_3 (and_3_out, xor_2_out, xor_3_out);
  xor xor_3 (xor_3_out, demultiplexer_2_out1[23], demultiplexer_3_out1[23]);
  or or_3 (comparator_1_eq[2], adder_1_cout, subtractor_1_bout);
  Adder #(.width(24)) adder_1 (
    .a(demultiplexer_2_out0), .b(demultiplexer_3_out0), .out(adder_1_out), .cin(and_2_out),
    .cout(adder_1_cout));
  Subtractor #(.width(24)) subtractor_1 (
    .a(demultiplexer_2_out1), .b(demultiplexer_3_out1), .out(subtractor_1_out), .bin(and_2_out),
    .bout(subtractor_1_bout));
  assign and_4_out = demultiplexer_2_out2 & demultiplexer_3_out2;  // AND_Gate and_4, 24 bits wide
  assign or_4_out = demultiplexer_2_out3 | demultiplexer_3_out3;  // OR_Gate or_4, 24 bits wide
  assign xor_4_out = demultiplexer_2_out4 ^ demultiplexer_3_out4;  // XOR_Gate xor_4, 24 bits wide
  assign not_1_out = ~demultiplexer_2_out5;  // NOT_Gate not_1, 24 bits wide
  Shifter #(.width(24)) shifter_1 (.in(demultiplexer_2_out6), .\dist (demultiplexer_3_out6), .out(shifter_1_out));
  Shifter #(.shift("lr"), .width(24)) shifter_2 (
    .in(demultiplexer_2_out7), .\dist (demultiplexer_3_out7), .out(shifter_2_out));
  Comparator #(.mode("unsigned"), .width(24)) comparator_1 (
    .a(multiplexer_1_out), .b({24{1'b0}}), .eq(comparator_1_eq[1]));  // open: gt, lt
  Multiplexer #(.select(3), .width(24)) multiplexer_1 (
    .in0(adder_1_out), .in1(subtractor_1_out), .in2(and_4_out), .in3(or_4_out), .in4(xor_4_out),
    .in5(not_1_out), .in6(shifter_1_out), .in7(shifter_2_out), .out(multiplexer_1_out),
    .sel(demultiplexer_4_out1[6:4]));
  Register #(.width(4)) FLAGS (
    .D({comparator_1_eq, multiplexer_1_out[23]}), .en(demultiplexer_4_out1[2]), .Q(FLAGS_q),
    .clk(clock_1_out), .clr(GLOBAL_RESET_out));
  Adder #(.width(24)) adder_2 (.a(24'h1), .b(counter_1_q), .out(adder_2_out));  // open: cin, cout
  Multiplexer #(.select(4), .width(24)) multiplexer_2 (
    .in0(R0_q), .in1(R1_q), .in2(R2_q), .in3(R3_q), .in4(R4_q), .in5(R5_q), .in6(R6_q), .in7(R7_q),
    .in8(R8_q), .in9(R9_q), .in10(R10_q), .in11(R11_q), .in12(R12_q), .in13(R13_q), .in14(R14_q),
    .in15(R15_q), .out(multiplexer_2_out), .sel(CODE_ROM_data_6[17:14]));
  Multiplexer #(.select(4), .width(24)) multiplexer_3 (
    .in0(R0_q), .in1(R1_q), .in2(R2_q), .in3(R3_q), .in4(R4_q), .in5(R5_q), .in6(R6_q), .in7(R7_q),
    .in8(R8_q), .in9(R9_q), .in10(R10_q), .in11(R11_q), .in12(R12_q), .in13(R13_q), .in14(R14_q),
    .in15(R15_q), .out(multiplexer_3_out), .sel(CODE_ROM_data_6[21:18]));
  Multiplexer #(.select(2)) multiplexer_4 (
    .in0(FLAGS_q[0]), .in1(FLAGS_q[1]), .in2(FLAGS_q[2]), .in3(FLAGS_q[3]), .out(multiplexer_4_out),
    .sel(demultiplexer_4_out3_2));
  Multiplexer #(.select(2)) multiplexer_5 (
    .in0(FLAGS_q[0]), .in1(FLAGS_q[1]), .in2(FLAGS_q[2]), .in3(FLAGS_q[3]), .out(multiplexer_5_out),
    .sel(demultiplexer_4_out3_2));
  RAM #(.clearpin("true"), .dataWidth(24), .enables("line")) STACK (
    .addr(STACK_POINTER_q), .we(demultiplexer_4_out3[2]), .clk(clock_1_out), .din(adder_2_out),
    .dout(STACK_dout), .clr(GLOBAL_RESET_out));
  Counter STACK_POINTER (
    .count(demultiplexer_4_out3[4]), .Q(STACK_POINTER_q), .up(demultiplexer_4_out3[3]), .clk(clock_1_out),
    .clr(GLOBAL_RESET_out));  // open: load, D, carry
  Multiplexer multiplexer_6 (
    .in0(multiplexer_4_out), .in1(not_2_out), .out(multiplexer_6_out), .sel(demultiplexer_4_out3[6]));
  not not_2 (not_2_out, multiplexer_5_out);
  RAM #(.addrWidth(24), .clearpin("true"), .dataWidth(24), .enables("line")) GEN_RAM (
    .addr(controlled_buffer_3_out), .we(demultiplexer_4_out2[1]), .clk(clock_1_out),
    .din(controlled_buffer_4_out), .dout(GEN_RAM_dout), .clr(GLOBAL_RESET_out));
  assign controlled_buffer_3_out = demultiplexer_4_out2[2] ? multiplexer_2_out : 24'bz;  // Controlled_Buffer controlled_buffer_3
  assign controlled_buffer_4_out = demultiplexer_4_out2[2] ? multiplexer_3_out : 24'bz;  // Controlled_Buffer controlled_buffer_4
  Demultiplexer #(.select(3), .width(9)) demultiplexer_4 (
    .out1(demultiplexer_4_out1),
    .out2({demultiplexer_4_out2[8:5], demultiplexer_4_out2_2, demultiplexer_4_out2[2:0]}),
    .out3({demultiplexer_4_out3_2, demultiplexer_4_out3}), .out4(demultiplexer_4_out4), .in(CODE_ROM_data_3),
    .sel(CODE_ROM_data_7));  // open: out0, out5, out6, out7
  and and_5 (and_5_out, demultiplexer_4_out3[5], multiplexer_6_out);
  or or_5 (or_5_out, and_5_out, demultiplexer_4_out3[0]);
  Multiplexer #(.width(24)) multiplexer_7 (
    .in0(CODE_ROM_data), .in1(STACK_dout), .out(multiplexer_7_out), .sel(demultiplexer_4_out3[1]));
  Counter #(.max('hffffff), .width(24)) counter_1 (
    .load(or_5_out), .D(multiplexer_7_out), .count(multiplexer_8_out), .Q(counter_1_q), .up(1'b1),
    .clk(clock_1_out), .clr(GLOBAL_RESET_out));  // open: carry
  Multiplexer multiplexer_8 (
    .in0(1'b1), .in1(multiplexer_9_out), .out(multiplexer_8_out), .sel(demultiplexer_4_out4[0]));
  Multiplexer multiplexer_9 (
    .in0(OFFSET_X_carry), .in1(OFFSET_Y_carry), .out(multiplexer_9_out), .sel(demultiplexer_4_out4[1]));
  Multiplexer #(.select(3), .width(24)) multiplexer_10 (
    .in0(multiplexer_1_out), .in1(multiplexer_2_out), .in2(GEN_RAM_dout), .in3(CODE_ROM_data),
    .in4(bit_extender_3_out),
    .out({multiplexer_10_out_3, multiplexer_10_out_2[7:4], multiplexer_10_out[9:7], multiplexer_10_out_2[3:0], multiplexer_10_out[2:0]}),
    .sel(CODE_ROM_data_4));  // open: in5, in6, in7
  ROM #(.addrWidth(24), .dataWidth(64)) CODE_ROM (
    .addr(counter_1_q),
    .data({CODE_ROM_data_8, CODE_ROM_data_7, CODE_ROM_data_6, CODE_ROM_data_5, CODE_ROM_data_4, CODE_ROM_data_3, CODE_ROM_data_2, CODE_ROM_data}));
  or or_6 (or_6_out, demultiplexer_4_out1[7], demultiplexer_4_out2_2[0]);
  Register TILE_OFFSET (
    .D(multiplexer_10_out_2), .en(or_6_out), .Q(TILE_OFFSET_q), .clk(clock_1_out), .clr(GLOBAL_RESET_out));
  assign bit_extender_1_out = {{1{1'b0}}, OFFSET_X_q_2};  // Bit_Extender bit_extender_1
  Adder #(.width(4)) adder_3 (
    .a(bit_extender_1_out), .b(TILE_OFFSET_q[3:0]), .out(adder_3_out), .cin(adder_5_cout));  // open: cout
  assign bit_extender_2_out = {{1{1'b0}}, OFFSET_Y_q_2};  // Bit_Extender bit_extender_2
  Adder #(.width(4)) adder_4 (
    .a(bit_extender_2_out), .b(TILE_OFFSET_q[7:4]), .out(adder_4_out), .cin(adder_6_cout));  // open: cout
  or or_7 (or_7_out, demultiplexer_4_out1[8], demultiplexer_4_out2_2[1]);
  Register RINPT (.D(A_out), .en(1'b1), .Q(RINPT_q), .clk(clock_1_out), .clr(GLOBAL_RESET_out));
  Multiplexer #(.width(8)) multiplexer_11 (
    .in0({adder_4_out, adder_3_out}),
    .in1({multiplexer_10_out[7], multiplexer_10_out_2[3:0], multiplexer_10_out[2:0]}),
    .out(multiplexer_11_out), .sel(or_7_out));
  Demultiplexer demultiplexer_5 (.out0(demultiplexer_5_out0), .out1(demultiplexer_5_out1), .in(1'b1), .sel(or_7_out));
  assign bit_extender_3_out = {{16{1'b0}}, RINPT_q};  // Bit_Extender bit_extender_3
  Button LEFT (.out(A_out[5]));
  RAM #(.clearpin("true"), .dataWidth(16)) TILE_BUFFER (
    .addr(multiplexer_11_out), .we(demultiplexer_5_out1), .oe(demultiplexer_5_out0), .clk(clock_1_out),
    .din({multiplexer_10_out_3, multiplexer_10_out_2[7:4], multiplexer_10_out[9:8]}),
    .dout(TILE_BUFFER_dout), .clr(GLOBAL_RESET_out));
  Register #(.width(6)) PIXEL_OFFSET (
    .D({multiplexer_10_out[9:7], multiplexer_10_out[2:0]}), .en(or_6_out), .Q(PIXEL_OFFSET_q),
    .clk(clock_1_out), .clr(GLOBAL_RESET_out));
  Button UP (.out(A_out[4]));
  Button RIGHT (.out(A_out[6]));
  Button DOWN (.out(A_out[7]));
  Button B (.out(A_out[1]));
  Adder #(.width(3)) adder_5 (
    .a(OFFSET_X_q), .b(PIXEL_OFFSET_q[2:0]), .out(adder_5_out), .cout(adder_5_cout));  // open: cin
  Adder #(.width(3)) adder_6 (
    .a(OFFSET_Y_q), .b(PIXEL_OFFSET_q[5:3]), .out(adder_6_out), .cout(adder_6_cout));  // open: cin
  Button Y (.out(A_out[3]));
  Button X (.out(A_out[2]));
  Button A (.out(A_out[0]));
  assign bit_extender_4_out = {{10{1'b0}}, {adder_6_out, adder_5_out}};  // Bit_Extender bit_extender_4
  ROM #(.addrWidth(4), .dataWidth(16)) LUT (.addr(RESOURCES_data), .data(LUT_data));
  Shifter #(.width(16)) shifter_3 (.in(TILE_BUFFER_dout), .\dist (4'b0110), .out(shifter_3_out));
  Adder #(.width(16)) adder_7 (.a(shifter_3_out), .b(bit_extender_4_out), .out(adder_7_out));  // open: cin, cout
  Counter #(.max('h3f), .width(6)) OFFSET_X (
    .count(demultiplexer_5_out0), .Q({OFFSET_X_q_2, OFFSET_X_q}), .carry(OFFSET_X_carry), .clk(clock_1_out),
    .clr(GLOBAL_RESET_out));  // open: load, D, up
  ROM #(.addrWidth(16), .dataWidth(4)) RESOURCES (.addr(adder_7_out), .data(RESOURCES_data));
  Counter #(.max('h3f), .width(6)) OFFSET_Y (
    .count(OFFSET_X_carry), .Q({OFFSET_Y_q_2, OFFSET_Y_q}), .carry(OFFSET_Y_carry), .clk(clock_1_out),
    .clr(GLOBAL_RESET_out));  // open: load, D, up
  // RGB_Video #(.cursor("No Cursor"), .height(64), .scale(3), .width(64)) rgb_video_1: pin names not known; wires that end beside it: clock_1_out, GLOBAL_RESET_out, GLOBAL_RESET_out, clock_1_out, 1'b1, {OFFSET_X_q_2, OFFSET_X_q}, {OFFSET_Y_q_2, OFFSET_Y_q}, LUT_data

  // Notes on the sheet:
  //   BUS_A
  //   REGS_CONTROL
  //   BUS B
  //   ALU_CONTROL
  //   REGS_DATA_IN
  //   FINE_CONTROL
  //   OPCODE
  //   contents of CODE_ROM (hex, n*v repeats v):
  //   800080100000000 840060100000000 880060100000001 4c8002700000000 c0000a000000007 840060100000100
  //   c00000100000029 880060100000002 4c8002700000000 c0000a00000000c 840060100000200 c00000100000029
  //   880060100000004 4c8002700000000 c0000a000000011 840060100001800 c00000100000029 880060100000008
  //   4c8002700000000 c0000a000000016 840060100001900 c00000100000029 880060100000010 4c8002700000000
  //   c0000a00000001b 840060100001500 c00000100000029 880060100000020 4c8002700000000 c0000a000000020
  //   840060100000c00 c00000100000029 880060100000040 4c8002700000000 c0000a000000025 840060100001200
  //   c00000100000029 880060100000080 4c8002700000000 c0000a000000029 840060100000400 1000000300000000
  //   800421000000000 c00000100000000
  //   contents of LUT (hex, n*v repeats v):
  //   18e5 592b b1ea ebea fe6e a78e 3dac 238f 29ad 3af9 453e 777e f7be 9598 5370 31ea
  //   contents of RESOURCES (hex, n*v repeats v):
  //   74*0 4*c 0 0 0 c 4*0 c 0 0 c 4*0 c 0 0 c 4*0 c 0 0 6*c 0 0 c 4*0 c 0 0 c 4*0 c 10*0 5*c 0 0 0 c 4*0
  //   c 0 0 c 4*0 c 0 0 5*c 0 0 0 c 4*0 c 0 0 c 4*0 c 0 0 5*c 12*0 4*c 0 0 0 c 4*0 c 0 0 c 7*0 c 7*0 c 7*0
  //   c 4*0 c 0 0 0 4*c 11*0 5*c 0 0 0 c 4*0 c 0 0 c 4*0 c 0 0 c 4*0 c 0 0 c 4*0 c 0 0 c 4*0 c 0 0 5*c
  //   11*0 5*c 0 0 0 c 7*0 c 7*0 5*c 0 0 0 c 7*0 c 7*0 5*c 11*0 5*c 0 0 0 c 7*0 c 7*0 4*c 4*0 c 7*0 c 7*0
  //   c 16*0 c c c 4*0 c 0 0 0 c 0 0 0 c 7*0 c 0 c c c 0 0 0 c 0 0 0 c 0 0 0 c 0 0 0 c 4*0 c c c 12*0 c 0
  //   0 0 c 0 0 0 c 0 0 0 c 0 0 0 c 0 0 0 c 0 0 0 5*c 0 0 0 c 0 0 0 c 0 0 0 c 0 0 0 c 0 0 0 c 0 0 0 c 11*0
  //   5*c 5*0 c 7*0 c 7*0 c 7*0 c 7*0 c 5*0 5*c 11*0 5*c 7*0 c 7*0 c 7*0 c 7*0 c 0 0 0 c 0 0 0 c 4*0 c c c
  //   12*0 c 0 0 0 c 0 0 0 c 0 0 c 4*0 c 0 c 5*0 c c 6*0 c 0 c 5*0 c 0 0 c 4*0 c 0 0 0 c 11*0 c 7*0 c 7*0
  //   c 7*0 c 7*0 c 7*0 c 7*0 5*c 11*0 c 0 0 0 c 0 0 0 c c 0 c c 0 0 0 c 0 c 0 c 0 0 0 c 0 0 0 c 0 0 0 c 0
  //   0 0 c 0 0 0 c 0 0 0 c 0 0 0 c 0 0 0 c 11*0 c 0 0 0 c 0 0 0 c c 0 0 c 0 0 0 c c 0 0 c 0 0 0 c 0 c 0 c
  //   0 0 0 c 0 c 0 c 0 0 0 c 0 0 c c 0 0 0 c 0 0 c c 12*0 c c c 4*0 c 0 0 0 c 0 0 0 c 0 0 0 c 0 0 0 c 0 0
  //   0 c 0 0 0 c 0 0 0 c 0 0 0 c 0 0 0 c 4*0 c c c 12*0 4*c 4*0 c 0 0 0 c 0 0 0 c 0 0 0 c 0 0 0 c 0 0 0 c
  //   0 0 0 4*c 4*0 c 7*0 c 16*0 c c c 4*0 c 0 0 0 c 0 0 0 c 0 0 0 c 0 0 0 c 0 0 0 c 0 0 0 c 0 0 0 c 0 0 0
  //   c 0 0 c c 4*0 5*c 10*0 4*c 4*0 c 0 0 0 c 0 0 0 c 0 0 0 c 0 0 0 4*c 4*0 c 0 0 0 c 0 0 0 c 0 0 0 c 0 0
  //   0 c 0 0 0 c 12*0 c c c 4*0 c 0 0 0 c 0 0 0 c 8*0 c c c 8*0 c 0 0 0 c 0 0 0 c 4*0 c c c 12*0 5*c 5*0
  //   c 7*0 c 7*0 c 7*0 c 7*0 c 7*0 c 13*0 c 0 0 0 c 0 0 0 c 0 0 0 c 0 0 0 c 0 0 0 c 0 0 0 c 0 0 0 c 0 0 0
  //   c 0 0 0 c 0 0 0 c 0 0 0 c 4*0 c c c 12*0 c 0 0 0 c 0 0 0 c 0 0 0 c 0 0 0 c 0 0 0 c 0 0 0 c 0 0 0 c
  //   4*0 c 0 c 5*0 c 0 c 6*0 c 13*0 c 0 c 0 c 0 0 0 c 0 c 0 c 0 0 0 c 0 c 0 c 0 0 0 c 0 c 0 c 0 0 0 c 0 c
  //   0 c 0 0 0 c 0 c 0 c 4*0 c 0 c 12*0 c 0 0 0 c 0 0 0 c 0 0 0 c 4*0 c 0 c 6*0 c 6*0 c 0 c 4*0 c 0 0 0 c
  //   0 0 0 c 0 0 0 c 11*0 c 0 0 0 c 0 0 0 c 0 0 0 c 0 0 0 c 0 0 0 c 4*0 c 0 c 6*0 c 7*0 c 7*0 c 13*0 5*c
  //   7*0 c 6*0 c 6*0 c 6*0 c 6*0 c 7*0 5*c
endmodule
